# Fritzing sketch tugas (saved by Fritzing 0.9.0b)
breadboards: 1

parts:
  PIR1 = PIR sensor
  Composant1 = Arduino Uno (Rev3)

nets:
  VDD: PIR1.VDD, Composant1.5V
  N1: PIR1.SIG, Composant1.D8
  GND: PIR1.GND, Composant1.GND

// code stored in the sketch: pir_sensor.ino
/*Ahram Canadian University
Course project*/
int pir =2;
int pirState;
int red1=3;
int red2=4;
int green=5;
int pushbutton1=6;
int pushbutton2=7;
int pushbutton3=8;
int count1;
int count2;
int count3;
int speaker=9;


void setup() {
  // put your setup code here, to run once:
  pinMode(pir, INPUT);
  pinMode(red1, OUTPUT);
  pinMode(red2, OUTPUT);
  pinMode(green, OUTPUT);
  pinMode(pushbutton1, INPUT);
  pinMode(pushbutton2, INPUT);
  pinMode(pushbutton3, INPUT);
  pinMode(speaker, OUTPUT);
  pirState=LOW;
}

void loop() {
  // put your main code here, to run repeatedly:
  
  pirState = digitalRead(pir);
  
  if(pirState==HIGH){
    if(count1==1&&count2==2&&count3==1;){
        stopalarm();
        count1=0;
        count2=0;
        count3=0;
      }
      else{
        alarm();
        if(digitalRead(pushbutton1)==LOW){
            count1=1;
          }
        else if(digitalRead(pushbutton2)==LOW){
            count2+=1;
          }
        else if(digitalRead(pushbutton3)==LOW){
            count3=1;      
          }
      } 
  }
  else{
    stopalarm();
  }      
}
void alarm(long duration, int frequency){
  
  digitalWrite(red1, HIGH);
  delay(200);
  digitalWrite(red2, HIGH);
  delay(200);
  play(duration, frequency);
}

void play(long duration, int frequency){
  duration = duration*1000;
  int period = (1.0/frequency)*1000000;
  long elapsed = 0;
  while(elapsed<duration){
    digitalWrite(speaker, HIGH);
    delayMicroseconds(period/2);
    digitalWrite(speaker, LOW);
    delayMicroseconds(period/2);
    elapsed+= period;
  }
}

void stopalarm(){
  digitalWrite(red1, LOW);
  digitalWrite(red2, LOW);
  digitalWrite(green, HIGH); 
  delay(500);
}
